// Logisim project 3BitCounter_Agnes_Duru_2.circ as structural Verilog: 1 circuit, main circuit main
module main (
  input  in_1
);

  wire Clock_out, Jb, Jc, not_1_out, not_2_out, nQa, nQaD_out, nQanQb_out, nQanQbD_out, nQb, nQc, Qa,
       QanD_out, QaQb_out, QaQbnD_out, Qb, Qc, undriven, undriven_2;

  not not_1 (not_1_out, in_1);
  not not_2 (not_2_out, in_1);
  and nQanQb (nQanQb_out, nQa, nQb);
  and QaQb (QaQb_out, Qa, Qb);
  and nQanQbD (nQanQbD_out, nQanQb_out, in_1);
  or or_1 (Jc, nQanQbD_out, QaQbnD_out);
  and QaQbnD (QaQbnD_out, QaQb_out, not_1_out);
  and QanD (QanD_out, Qa, not_2_out);
  or or_2 (Jb, QanD_out, nQaD_out);
  and nQaD (nQaD_out, nQa, in_1);
  Clock Clock (.out(Clock_out));
  J_K_Flip_Flop j_k_ff_1 (.J(Jc), .K(Jc), .clk(Clock_out), .Q(Qc), .Qn(nQc), .reset(undriven));  // open: preset
  J_K_Flip_Flop j_k_ff_2 (.J(Jb), .K(Jb), .clk(Clock_out), .Q(Qb), .Qn(nQb), .preset(undriven), .reset(undriven_2));
  J_K_Flip_Flop j_k_ff_3 (.J(1'b1), .K(1'b1), .clk(Clock_out), .Q(Qa), .Qn(nQa), .preset(undriven_2));  // open: reset
  Hex_Digit_Display hex_digit_display_1 (.value({1'b0, Qc, Qb, Qa}));  // open: dp

  // Other names for the same wires on the sheet: Kb = Jb; Kc = Jc
endmodule
